# Fritzing sketch testbench (saved by Fritzing 0.9.3b)
breadboards: 1

parts:
  U1 = LCD-16X2 [package=lcd-16x2_noholes]
  S1 = Pushbutton [package="[SMD]"]
  S2 = Pushbutton [package="[SMD]"]
  R1 = Resistor [tolerance=±5% resistance=4.7k package="0603 [SMD]"]
  R2 = Resistor [tolerance=±5% resistance=4.7k package="0603 [SMD]"]
  WeMos_D1_Mini2 = WeMos D1 Mini  # not connected
  R3 = Resistor [tolerance=±5% resistance=4.7k package="0603 [SMD]"]
  R4 = Resistor [tolerance=±5% resistance=2.2k package="0603 [SMD]"]
  R5 = Resistor [tolerance=±5% resistance=1k package="0603 [SMD]"]

nets:
  N1: U1.VSS, U1.VO, U1.R_W, U1.K, R1.Pin_1, R2.Pin_1, R4.Pin_0, R5.Pin_0
  N2: U1.VDD, U1.A, S1.Pin_1, S1.Pin_2, S2.Pin_1, S2.Pin_2, R3.Pin_0
  N3: S1.Pin_3, S1.Pin_4, R1.Pin_0
  N4: S2.Pin_3, S2.Pin_4, R2.Pin_0
  N5: R3.Pin_1, R4.Pin_1
